// Logisim project Labor4_Pfennig_Bissendorf.circ as structural Verilog: 4 circuits, main circuit ALU
module ALU (
  input  [7:0] A,
  input  [7:0] B,
  input  [2:0] OpCode,
  output [7:0] C,
  output zero
);

  wire or_2_out;
  wire [7:0] adder_1_out, adder_2_out, adder_3_out, and_1_out, or_1_out, pull_resistor_1_node,
       subtractor_1_out;

  Pull_Resistor #(.pull(1)) pull_resistor_1 (.node(pull_resistor_1_node[0]));
  Pull_Resistor pull_resistor_2 (.node(pull_resistor_1_node[7]));
  Adder adder_1 (
    .a(A), .b({{7{pull_resistor_1_node[7]}}, pull_resistor_1_node[0]}), .out(adder_1_out));  // open: cin, cout
  Adder adder_2 (
    .a(B), .b({{7{pull_resistor_1_node[7]}}, pull_resistor_1_node[0]}), .out(adder_2_out));  // open: cin, cout
  Adder adder_3 (.a(A), .b(B), .out(adder_3_out));  // open: cin, cout
  Subtractor subtractor_1 (.a(A), .b(B), .out(subtractor_1_out));  // open: bin, bout
  assign and_1_out = A & B;  // AND_Gate and_1, 8 bits wide
  assign or_1_out = A | B;  // OR_Gate or_1, 8 bits wide
  Multiplexer #(.select(3), .width(8)) multiplexer_1 (
    .in0(A), .in1(B), .in2(adder_1_out), .in3(adder_2_out), .in4(adder_3_out), .in5(subtractor_1_out),
    .in6(and_1_out), .in7(or_1_out), .out(C), .sel(OpCode));
  or or_2 (or_2_out, C[0], C[1], C[2], C[3], C[4], C[5], C[6], C[7]);
  not not_1 (zero, or_2_out);
endmodule

module main (
  input  [7:0] in_1,
  output [7:0] out_2
);

  wire button_1_out, clk, mikroprogrammspeicher_1_addr_mux, mikroprogrammspeicher_1_en_a,
       mikroprogrammspeicher_1_en_b, mikroprogrammspeicher_1_en_mbr, mikroprogrammspeicher_1_en_out,
       mikroprogrammspeicher_1_en_pc, mikroprogrammspeicher_1_en_zero, mikroprogrammspeicher_1_siz,
       mikroprogrammspeicher_1_write_enable;
  wire [1:0] mikroprogrammspeicher_1_mux_select;
  wire [2:0] mikroprogrammspeicher_1_alu;
  wire [4:0] cpu_1_external_memory_byte_out;
  wire [7:0] cpu_1_external_memory_outtput_bus, multiplexer_1_out, ram_1_dout;
  wire [7:5] cpu_1_external_memory_byte_out_2;

  Button button_1 (.out(button_1_out));
  Multiplexer #(.width(8)) multiplexer_1 (
    .in0(cpu_1_external_memory_outtput_bus),
    .in1({cpu_1_external_memory_byte_out_2, cpu_1_external_memory_byte_out}), .out(multiplexer_1_out),
    .sel(mikroprogrammspeicher_1_addr_mux));
  Clock clock_1 (.out(clk));
  RAM #(.trigger("falling")) ram_1 (
    .addr(multiplexer_1_out), .we(mikroprogrammspeicher_1_write_enable), .oe(1'b1), .clk(clk), .din(out_2),
    .dout(ram_1_dout));
  Mikroprogrammspeicher mikroprogrammspeicher_1 (
    .in_put(cpu_1_external_memory_byte_out), .clk(clk), .reset(button_1_out),
    .EN_PC(mikroprogrammspeicher_1_en_pc), .mux_select(mikroprogrammspeicher_1_mux_select),
    .alu(mikroprogrammspeicher_1_alu), .EN_B(mikroprogrammspeicher_1_en_b),
    .EN_OUT(mikroprogrammspeicher_1_en_out), .EN_MBR(mikroprogrammspeicher_1_en_mbr),
    .EN_A(mikroprogrammspeicher_1_en_a), .EN_ZERO(mikroprogrammspeicher_1_en_zero),
    .SIZ(mikroprogrammspeicher_1_siz), .write_enable(mikroprogrammspeicher_1_write_enable),
    .addr_mux(mikroprogrammspeicher_1_addr_mux));
  cpu cpu_1 (
    .External_Memory_Data_Bus(ram_1_dout), .Internal_Input_Bus(in_1), .Opcode(mikroprogrammspeicher_1_alu),
    .clk(clk), .reset(button_1_out), .Mux_select(mikroprogrammspeicher_1_mux_select),
    .Enable_A(mikroprogrammspeicher_1_en_a), .Enable_B(mikroprogrammspeicher_1_en_b),
    .Enable_MBR(mikroprogrammspeicher_1_en_mbr), .ENABLE_PC(mikroprogrammspeicher_1_en_pc),
    .en_out(mikroprogrammspeicher_1_en_out), .en_zero(mikroprogrammspeicher_1_en_zero),
    .SIZ(mikroprogrammspeicher_1_siz), .Output_Bus(out_2),
    .External_Memory_Byte_Out({cpu_1_external_memory_byte_out_2, cpu_1_external_memory_byte_out}),
    .External_Memory_Outtput_Bus(cpu_1_external_memory_outtput_bus));
endmodule

module Mikroprogrammspeicher (
  input  [4:0] in_put,
  input  clk,
  input  reset,
  output EN_PC,
  output [1:0] mux_select,
  output [2:0] alu,
  output EN_B,
  output EN_OUT,
  output EN_MBR,
  output EN_A,
  output EN_ZERO,
  output SIZ,
  output write_enable,
  output addr_mux
);

  wire [4:0] multiplexer_1_out;
  wire [15:10] MIR_q;
  wire [19:0] MCS_data;

  Multiplexer #(.width(5)) multiplexer_1 (.in0(MIR_q[15:11]), .in1(in_put), .out(multiplexer_1_out), .sel(MIR_q[10]));
  Register #(.width(5)) MPC (.en(1'b1), .clk(clk), .clr(reset));  // open: D, Q
  ROM #(.addrWidth(5), .dataWidth(20)) MCS (.addr(multiplexer_1_out), .data(MCS_data));
  Register #(.trigger("falling"), .width(20)) MIR (
    .D(MCS_data), .en(1'b1), .clk(clk),
    .Q({addr_mux, write_enable, EN_ZERO, SIZ, MIR_q, alu, EN_A, EN_B, EN_MBR, EN_PC, EN_OUT, mux_select}),
    .clr(reset));

  // Notes on the sheet:
  //   contents of MCS (hex, n*v repeats v):
  //   fc10 18a 208c3 20804 298a 3010 89 2418a 24810 208c1 20940 20820 20a40 208a3 20884 209a0 208c0 20bc0
  //   20b40 20ac0 a98a b010 b98a 10089 c98a d010 c0800 2e18a 2e810 af010 208c1 2f800
endmodule

module cpu (
  input  [7:0] External_Memory_Data_Bus,
  input  [7:0] Internal_Input_Bus,
  input  [2:0] Opcode,
  input  clk,
  input  reset,
  input  [1:0] Mux_select,
  input  Enable_A,
  input  Enable_B,
  input  Enable_MBR,
  input  ENABLE_PC,
  input  en_out,
  input  en_zero,
  input  SIZ,
  output [7:0] Output_Bus,
  output [7:0] External_Memory_Byte_Out,
  output [7:0] External_Memory_Outtput_Bus
);

  wire alu_1_zero, En_a, En_b, En_mbr, En_out_t, En_pc, nand_1_out, zero;
  wire [7:0] A_q, alu_1_c, B_q, multiplexer_1_out;

  nand nand_1 (nand_1_out, SIZ, zero);
  and and_1 (En_a, nand_1_out, Enable_A);
  Register PC (.D(alu_1_c), .en(En_pc), .clk(clk), .Q(External_Memory_Outtput_Bus), .clr(reset));
  and and_2 (En_b, nand_1_out, Enable_B);
  Register A (.D(alu_1_c), .en(En_a), .clk(clk), .Q(A_q), .clr(reset));
  Register B (.D(alu_1_c), .en(En_b), .clk(clk), .Q(B_q), .clr(reset));
  Register MBR (.D(External_Memory_Data_Bus), .en(En_mbr), .clk(clk), .Q(External_Memory_Byte_Out), .clr(reset));
  and and_3 (En_mbr, nand_1_out, Enable_MBR);
  and and_4 (En_pc, nand_1_out, ENABLE_PC);
  Multiplexer #(.select(2), .width(8)) multiplexer_1 (
    .in0(B_q), .in1(External_Memory_Byte_Out), .in2(External_Memory_Outtput_Bus), .in3(Internal_Input_Bus),
    .out(multiplexer_1_out), .sel(Mux_select));
  and and_5 (En_out_t, nand_1_out, en_out);
  ALU alu_1 (.A(A_q), .B(multiplexer_1_out), .OpCode(Opcode), .C(alu_1_c), .zero(alu_1_zero));
  Register out_put (.D(alu_1_c), .en(En_out_t), .clk(clk), .Q(Output_Bus), .clr(reset));
  Register #(.width(1)) zero_reg (.D(alu_1_zero), .en(en_zero), .clk(clk), .Q(zero), .clr(reset));
endmodule
